// Logisim project brainfuck.circ as structural Verilog: 5 circuits, main circuit main
module main (
);

  wire and_1_out, and_2_out, and_3_out, and_4_out, and_5_out, clock_1_out, counter_1_q, decoder_2_out2,
       decoder_2_out3, DisplayValue, ExecuteCLK, HasChar, InstructionCLK, MemCounterDown, MemCounterUp,
       MemoryWriteEnable, or_1_out, ReadChar;
  wire [2:0] Instruction;
  wire [6:0] decrease7_1_out_2, increase7_1_out_2, InputChar, multiplexer_1_out, Value;
  wire [15:0] decrease16_1_out_2, InstructionPointer_q, MemoryPointer_q;

  Clock clock_1 (.out(clock_1_out));
  and and_1 (and_1_out, clock_1_out, ~and_2_out);  // AND_Gate
  and and_2 (and_2_out, ReadChar, ~HasChar);  // AND_Gate
  TTY tty_1 (.data(Value), .clk(and_3_out));  // open: we, clr
  and and_3 (and_3_out, DisplayValue, ExecuteCLK);
  Keyboard keyboard_1 (.clk(InstructionCLK), .re(ReadChar), .avail(HasChar), .data(InputChar));  // open: clr
  Decoder #(.enable("false")) decoder_1 (.out0(InstructionCLK), .out1(ExecuteCLK), .sel(counter_1_q));
  Counter #(.max('h1), .width(1)) counter_1 (.Q(counter_1_q), .clk(and_1_out));  // open: load, D, count, carry, up, clr
  LED led_1 (.in(ReadChar));
  Counter #(.max('hffff), .width(16)) InstructionPointer (
    .Q(InstructionPointer_q), .clk(InstructionCLK));  // open: load, D, count, carry, up, clr
  ROM #(.addrWidth(16), .dataWidth(3)) Programm (.addr(InstructionPointer_q), .data(Instruction));
  INCREASE7 increase7_1 (.in_1(Value), .out_2(increase7_1_out_2));
  DECREASE7 decrease7_1 (.in_1(Value), .out_2(decrease7_1_out_2));
  or or_1 (or_1_out, MemCounterDown, MemCounterUp);
  Multiplexer #(.select(3), .width(7)) multiplexer_1 (
    .in2(increase7_1_out_2), .in3(decrease7_1_out_2), .in5(InputChar), .out(multiplexer_1_out),
    .sel(Instruction));  // open: in0, in1, in4, in6, in7
  Counter #(.max('hffff), .width(16)) MemoryPointer (
    .load(MemCounterDown), .D(decrease16_1_out_2), .count(or_1_out), .Q(MemoryPointer_q), .clk(and_4_out));  // open: carry, up, clr
  and and_4 (and_4_out, or_1_out, ExecuteCLK);
  and and_5 (and_5_out, MemoryWriteEnable, ExecuteCLK);
  DECREASE16 decrease16_1 (.in_1(MemoryPointer_q), .out_2(decrease16_1_out_2));
  RAM #(.addrWidth(16), .dataWidth(7), .enables("line")) Memory (
    .addr(MemoryPointer_q), .we(MemoryWriteEnable), .clk(and_5_out), .din(multiplexer_1_out), .dout(Value));
  Decoder #(.enable("false"), .select(3)) decoder_2 (
    .out0(MemCounterUp), .out1(MemCounterDown), .out2(decoder_2_out2), .out3(decoder_2_out3),
    .out4(DisplayValue), .out5(ReadChar), .sel(Instruction));  // open: out6, out7
  or or_2 (MemoryWriteEnable, decoder_2_out2, decoder_2_out3, ReadChar);

  // Notes on the sheet:
  //   Interrup if waiting for input
  //   contents of Programm (hex, n*v repeats v):
  //   5 0 5 1 4 0 4
endmodule

module INCREASE16 (
  input  [15:0] in_1,
  output [15:0] out_2
);

  Adder #(.width(16)) adder_1 (.a(in_1), .b(16'h1), .out(out_2));  // open: cin, cout
endmodule

module DECREASE16 (
  input  [15:0] in_1,
  output [15:0] out_2
);

  Subtractor #(.width(16)) subtractor_1 (.a(in_1), .b(16'h1), .out(out_2));  // open: bin, bout
endmodule

module DECREASE7 (
  input  [6:0] in_1,
  output [6:0] out_2
);

  Subtractor #(.width(7)) subtractor_1 (.a(in_1), .b(7'b0000001), .out(out_2));  // open: bin, bout
endmodule

module INCREASE7 (
  input  [6:0] in_1,
  output [6:0] out_2
);

  Adder #(.width(7)) adder_1 (.a(in_1), .b(7'b0000001), .out(out_2));  // open: cin, cout
endmodule
